// Digital circuit MemoryBank.dig as structural Verilog
module MemoryBank (
  input  [15:0] ADDR,
  input  nMemAccess,
  input  nMWrite,
  output [7:0] DATA
);

  wire MWrite, nCSRAM0, nCSRAM1, nCSRAM2, nCSROM;

  not not_1 (MWrite, nMWrite);
  _74139_RD _74139_rd_1 (
    .n1G(nMemAccess), ._1A(ADDR[14]), ._1B(ADDR[15]), .n2G(1'b1), ._2A(1'b0), ._2B(1'b0), .n1Y0(nCSRAM0),
    .n1Y1(nCSRAM1), .n1Y2(nCSRAM2), .n1Y3(nCSROM), .VCC(1'b1), .GND(1'b0));  // open: n2Y0, n2Y1, n2Y2, n2Y3
  RAMSinglePortSel #(.AddrBits(14), .Bits(8)) _16K (
    .A(ADDR[13:0]), .CS(~nCSRAM0), .WE(~nMWrite), .OE(~MWrite), .D(DATA));
  RAMSinglePortSel #(.AddrBits(14), .Bits(8)) _16K_2 (
    .A(ADDR[13:0]), .CS(~nCSRAM1), .WE(~nMWrite), .OE(~MWrite), .D(DATA));
  RAMSinglePortSel #(.AddrBits(14), .Bits(8)) _16K_3 (
    .A(ADDR[13:0]), .CS(~nCSRAM2), .WE(~nMWrite), .OE(~MWrite), .D(DATA));
  EEPROM #(.AddrBits(14), .Bits(8)) _16K_4 (.A(ADDR[13:0]), .CS(~nCSROM), .WE(1'b0), .OE(~1'b0), .D(DATA));

  // Other names for the same wires on the sheet: ADDR14[13:0] = ADDR[13:0]

  // Notes on the sheet:
  //   nMemAccess: default 1
  //   nMWrite: default 1
endmodule
