// Digital circuit PowerOnReset.dig as structural Verilog
module PowerOnReset (
  input  MSTRRST,
  input  CLK,
  output RESET,
  output nRESET
);

  wire _74161_rd_1_q0, _74161_rd_1_q1, _74161_rd_1_q2, and_1_out, nRST, POR_out;

  Reset #(.invertOutput("false")) POR (.out(POR_out));
  nor nor_1 (nRST, MSTRRST, POR_out);
  Break break_1 (.brk(POR_out));
  _74161_RD _74161_rd_1 (
    .A(1'b0), .B(1'b0), .C(1'b0), .D(1'b0), .nSPE(1'b1), .CP(CLK), .nMR(nRST), .PE(1'b1), .TE(1'b1),
    .Q0(_74161_rd_1_q0), .Q1(_74161_rd_1_q1), .Q2(_74161_rd_1_q2), .VCC(1'b1), .GND(1'b0));  // open: Q3, TC
  and and_1 (and_1_out, _74161_rd_1_q0, _74161_rd_1_q1, _74161_rd_1_q2);
  RS_FF_AS rs_ff_as_1 (.S(MSTRRST), .R(and_1_out), .Q(RESET), .nQ(nRESET));

  // Other names for the same wires on the sheet: RST = MSTRRST

  // Notes on the sheet:
  //   CLK: Hz: 8
endmodule
