// Digital circuit STRegister.dig as structural Verilog
module STRegister (
  input  [7:0] IN,
  input  nUpdateNZ,
  input  CP,
  input  nFlagInstr,
  input  [7:0] InstReg,
  input  CLK,
  input  [7:0] WBUS,
  input  nShiftRight,
  input  nUPDATEC,
  input  BREG0,
  input  nCarry8,
  input  nBITOP,
  input  BREG7,
  input  nSBC,
  input  BREG6,
  input  AREG7,
  input  SUM7,
  input  nUPDATEV,
  output [7:0] OUT
);

  wire _7474_rd_1__1q, _7474_rd_1__2q, _7474_rd_2__1q, _7474_rd_2__2q, _7474_rd_3__1q, _7474_rd_3__2q,
       _74138_rd_1_ny0, _74138_rd_1_ny1, _74138_rd_1_ny4, _74138_rd_1_ny5, _74257_rd_1_y1, _74257_rd_2_y1,
       _74257_rd_2_y2, _74574_rd_1_q0, _74574_rd_1_q1, _74574_rd_1_q5, equalszero_1_out, nClearCarry,
       nClearCarryRAW, nClearDecimal, nClearInterrupt, nClearNegative, nClearNegativeRAW, nClearOverflow,
       nClearOverflowRAW, nClearZero, nClearZeroRAW, not_1_out, not_2_out, not_3_out, not_4_out, not_5_out,
       not_6_out, nSetCarry, nSetCarryRAW, nSetDecimal, nSetInterrupt, nSetNegative, nSetNegativeRAW,
       nSetOverflow, nSetOverflowRAW, nSetZero, nSetZeroRAW, OVF, xor_1_out, xor_2_out, xor_3_out;

  not not_1 (not_1_out, nCarry8);
  _74257_RD _74257_rd_1 (
    .A1(BREG0), .A2(1'b0), .A3(1'b0), .A4(1'b0), .B1(not_1_out), .B2(1'b0), .B3(1'b0), .B4(1'b0),
    .S(nShiftRight), .nOE(1'b0), .Y1(_74257_rd_1_y1), .VCC(1'b1), .GND(1'b0));  // open: Y2, Y3, Y4
  not not_2 (not_2_out, _74257_rd_1_y1);
  or or_1 (nSetCarryRAW, nUPDATEC, not_2_out);
  or or_2 (nClearCarryRAW, nUPDATEC, _74257_rd_1_y1);
  not not_3 (not_3_out, nSBC);
  xor xor_1 (xor_1_out, not_3_out, BREG7);
  xor xor_2 (xor_2_out, xor_1_out, AREG7);
  xor xor_3 (xor_3_out, AREG7, SUM7);
  _74138_RD _74138_rd_1 (
    .A0(InstReg[5]), .A1(InstReg[6]), .A2(InstReg[7]), .G(1'b1), .nGB(CLK), .nGA(nFlagInstr),
    .nY0(_74138_rd_1_ny0), .nY1(_74138_rd_1_ny1), .nY2(nClearInterrupt), .nY3(nSetInterrupt),
    .nY4(_74138_rd_1_ny4), .nY5(_74138_rd_1_ny5), .nY6(nClearDecimal), .nY7(nSetDecimal), .VCC(1'b1),
    .GND(1'b0));
  _74574_RD _74574_rd_1 (
    .Q0(_74574_rd_1_q0), .Q1(_74574_rd_1_q1), .Q2(nSetZero), .Q3(nClearZero), .Q4(nSetOverflow),
    .Q5(_74574_rd_1_q5), .Q6(nSetNegative), .Q7(nClearNegative), .nOE(1'b0), .D0(nSetCarryRAW),
    .D1(nClearCarryRAW), .D2(nSetZeroRAW), .D3(nClearZeroRAW), .D4(nSetOverflowRAW), .D5(nClearOverflowRAW),
    .D6(nSetNegativeRAW), .D7(nClearNegativeRAW), .CLK(CLK), .VCC(1'b1), .GND(1'b0));
  EqualsZero equalszero_1 (.IN(WBUS), .OUT(equalszero_1_out));
  _74257_RD _74257_rd_2 (
    .A1(BREG7), .A2(BREG6), .A3(1'b0), .A4(1'b0), .B1(WBUS[7]), .B2(OVF), .B3(1'b0), .B4(1'b0), .S(nBITOP),
    .nOE(1'b0), .Y1(_74257_rd_2_y1), .Y2(_74257_rd_2_y2), .VCC(1'b1), .GND(1'b0));  // open: Y3, Y4
  xor xor_4 (OVF, xor_2_out, xor_3_out);
  not not_4 (not_4_out, _74257_rd_2_y2);
  not not_5 (not_5_out, equalszero_1_out);
  not not_6 (not_6_out, _74257_rd_2_y1);
  or or_3 (nClearZeroRAW, nUpdateNZ, not_5_out);
  or or_4 (nSetZeroRAW, nUpdateNZ, equalszero_1_out);
  or or_5 (nSetNegativeRAW, nUpdateNZ, not_6_out);
  or or_6 (nClearNegativeRAW, nUpdateNZ, _74257_rd_2_y1);
  or or_7 (nClearOverflowRAW, nUPDATEV, _74257_rd_2_y2);
  or or_8 (nSetOverflowRAW, nUPDATEV, not_4_out);
  and and_1 (nClearCarry, _74138_rd_1_ny0, _74574_rd_1_q1);
  and and_2 (nSetCarry, _74138_rd_1_ny1, _74574_rd_1_q0);
  and and_3 (nClearOverflow, _74138_rd_1_ny5, _74574_rd_1_q5);
  _7474_RD _7474_rd_1 (
    ._1Q(_7474_rd_1__1q), ._2Q(_7474_rd_1__2q), ._1nSET(nSetCarry), ._1D(IN[0]), ._1CLK(CP),
    ._1nCLR(nClearCarry), ._2nSET(nSetZero), ._2D(IN[1]), ._2CLK(CP), ._2nCLR(nClearZero), .VCC(1'b1),
    .GND(1'b0));  // open: _1nQ, _2nQ
  _7474_RD _7474_rd_2 (
    ._1Q(_7474_rd_2__1q), ._2Q(_7474_rd_2__2q), ._1nSET(nSetInterrupt), ._1D(IN[2]), ._1CLK(CP),
    ._1nCLR(nClearInterrupt), ._2nSET(nSetDecimal), ._2D(IN[3]), ._2CLK(CP), ._2nCLR(nClearDecimal),
    .VCC(1'b1), .GND(1'b0));  // open: _1nQ, _2nQ
  _7474_RD _7474_rd_3 (
    ._1Q(_7474_rd_3__1q), ._2Q(_7474_rd_3__2q), ._1nSET(nSetOverflow), ._1D(IN[6]), ._1CLK(CP),
    ._1nCLR(nClearOverflow), ._2nSET(nSetNegative), ._2D(IN[7]), ._2CLK(CP), ._2nCLR(nClearNegative),
    .VCC(1'b1), .GND(1'b0));  // open: _1nQ, _2nQ
  _74245_RD _74245_rd_1 (
    .nOE(1'b0), .DIR(1'b1), .A1(_7474_rd_1__1q), .A2(_7474_rd_1__2q), .A3(_7474_rd_2__1q),
    .A4(_7474_rd_2__2q), .A5(1'b0), .A6(1'b0), .A7(_7474_rd_3__1q), .A8(_7474_rd_3__2q), .B1(OUT[0]),
    .B2(OUT[1]), .B3(OUT[2]), .B4(OUT[3]), .B5(OUT[4]), .B6(OUT[5]), .B7(OUT[6]), .B8(OUT[7]), .VCC(1'b1),
    .GND(1'b0));

  // Other names for the same wires on the sheet: Carry = IN[0]; Zero = IN[1]; Interrupt = IN[2]; Decimal = IN[3];
  //   Overflow = IN[6]; Negative = IN[7]
endmodule
