// Digital circuit Sequencer.dig as structural Verilog
module Sequencer (
  input  CLK,
  input  [7:0] INSTR,
  input  [7:0] FLAGS,
  input  MSTRRST,
  output nALUOE,
  output nAREGOE,
  output nAREGCLK,
  output nBREGOE,
  output nBREGCLK,
  output nPCHOE,
  output nPCHCLK,
  output nSPREGOE,
  output nSPREGCLK,
  output nEBHOE,
  output nEBHCLK,
  output nPCLOE,
  output nPCLCLK,
  output nACCOE,
  output nACCCLK,
  output nEBLOE,
  output nEBLCLK,
  output nSTREGOE,
  output nSTREGCLK,
  output nEAHOE,
  output nEAHCLK,
  output nXREGOE,
  output nXREGCLK,
  output nYREGOE,
  output nYREGCLK,
  output nEALOE,
  output nEALCLK,
  output nCONSTOE,
  output [3:0] Constant,
  output [4:0] ALUOp,
  output nPCClockLow,
  output nPCClockHigh,
  output IREGLoad,
  output nMemAccess,
  output nMWrite,
  output nPCSel,
  output CarryZERO,
  output CarryONE,
  output nUpdateNZ,
  output nUpdateC,
  output nUpdateV,
  output NoBCD,
  output nFlagInst,
  output nShiftRight,
  output nSBC,
  output nBITOP,
  output [39:0] CtrlWord
);

  wire _74138_rd_1_ny0, _74138_rd_1_ny1, _74138_rd_1_ny2, _74138_rd_1_ny3, _74138_rd_1_ny4, _74138_rd_1_ny5,
       _74138_rd_1_ny6, _74138_rd_1_ny7, _74138_rd_2_ny0, _74138_rd_2_ny1, _74138_rd_2_ny2, _74138_rd_2_ny3,
       _74138_rd_2_ny4, _74138_rd_2_ny5, _74138_rd_2_ny6, _74138_rd_2_ny7, _74138_rd_3_ny0, _74138_rd_3_ny1,
       _74138_rd_3_ny2, _74138_rd_3_ny3, _74138_rd_3_ny4, _74138_rd_3_ny5, _74138_rd_3_ny6, _74138_rd_3_ny7,
       _74138_rd_4_ny0, _74138_rd_4_ny1, _74138_rd_4_ny2, _74138_rd_4_ny3, _74138_rd_4_ny4, _74138_rd_4_ny5,
       _74138_rd_4_ny6, _74138_rd_4_ny7, _74574_rd_2_q1, _74574_rd_3_q0, _74574_rd_4_q1, _74574_rd_4_q7,
       _74574_rd_8_q5, _74574_rd_8_q6, _74574_rd_8_q7, CLKLATCH, FLAG0, FLAG1, FLAG2, not_1_out, not_2_out,
       not_3_out, not_4_out, not_5_out, not_6_out, nSEQRST;
  wire [4:0] seqcounter_1_count;
  wire [13:13] _74151_rd_1_y;

  SeqCounter seqcounter_1 (.CLK(CLK), .RESET(MSTRRST), .nSEQRST(nSEQRST), .COUNT(seqcounter_1_count));
  _74151_RD _74151_rd_1 (
    .Y(_74151_rd_1_y[13]), .nG(1'b0), .D0(FLAGS[0]), .D1(FLAGS[1]), .D2(FLAGS[2]), .D3(FLAGS[3]),
    .D4(FLAGS[4]), .D5(FLAGS[5]), .D6(FLAGS[6]), .D7(FLAGS[7]), .A(FLAG0), .B(FLAG1), .C(FLAG2), .VCC(1'b1),
    .GND(1'b0));  // open: W
  // Probe Address on {_74151_rd_1_y[13], seqcounter_1_count, INSTR}
  MicrocodeROM microcoderom_1 (
    .ADDR({_74151_rd_1_y[13], seqcounter_1_count, INSTR}), .nCS(1'b0), .nOE(1'b0), .DATA(CtrlWord));
  _74138_RD _74138_rd_1 (
    .A0(CtrlWord[0]), .A1(CtrlWord[1]), .A2(CtrlWord[2]), .G(1'b1), .nGB(CtrlWord[3]), .nGA(1'b0),
    .nY0(_74138_rd_1_ny0), .nY1(_74138_rd_1_ny1), .nY2(_74138_rd_1_ny2), .nY3(_74138_rd_1_ny3),
    .nY4(_74138_rd_1_ny4), .nY5(_74138_rd_1_ny5), .nY6(_74138_rd_1_ny6), .nY7(_74138_rd_1_ny7), .VCC(1'b1),
    .GND(1'b0));
  _74138_RD _74138_rd_2 (
    .A0(CtrlWord[0]), .A1(CtrlWord[1]), .A2(CtrlWord[2]), .G(CtrlWord[3]), .nGB(1'b0), .nGA(1'b0),
    .nY0(_74138_rd_2_ny0), .nY1(_74138_rd_2_ny1), .nY2(_74138_rd_2_ny2), .nY3(_74138_rd_2_ny3),
    .nY4(_74138_rd_2_ny4), .nY5(_74138_rd_2_ny5), .nY6(_74138_rd_2_ny6), .nY7(_74138_rd_2_ny7), .VCC(1'b1),
    .GND(1'b0));
  _74138_RD _74138_rd_3 (
    .A0(CtrlWord[4]), .A1(CtrlWord[5]), .A2(CtrlWord[6]), .G(1'b1), .nGB(CtrlWord[7]), .nGA(1'b0),
    .nY0(_74138_rd_3_ny0), .nY1(_74138_rd_3_ny1), .nY2(_74138_rd_3_ny2), .nY3(_74138_rd_3_ny3),
    .nY4(_74138_rd_3_ny4), .nY5(_74138_rd_3_ny5), .nY6(_74138_rd_3_ny6), .nY7(_74138_rd_3_ny7), .VCC(1'b1),
    .GND(1'b0));
  _74138_RD _74138_rd_4 (
    .A0(CtrlWord[4]), .A1(CtrlWord[5]), .A2(CtrlWord[6]), .G(CtrlWord[7]), .nGB(1'b0), .nGA(1'b0),
    .nY0(_74138_rd_4_ny0), .nY1(_74138_rd_4_ny1), .nY2(_74138_rd_4_ny2), .nY3(_74138_rd_4_ny3),
    .nY4(_74138_rd_4_ny4), .nY5(_74138_rd_4_ny5), .nY6(_74138_rd_4_ny6), .nY7(_74138_rd_4_ny7), .VCC(1'b1),
    .GND(1'b0));
  Seven_Seg_Hex seven_seg_hex_1 (.d({1'b0, CtrlWord[26:24]}), .dp(1'b0));
  LED u_nPCSel (.in(not_1_out));
  not not_1 (not_1_out, CtrlWord[23]);
  LED u_nMWrite (.in(not_2_out));
  not not_2 (not_2_out, CtrlWord[22]);
  _74574_RD _74574_rd_1 (
    .Q0(nALUOE), .Q1(nAREGOE), .Q2(nBREGOE), .Q3(nPCHOE), .Q4(nSPREGOE), .Q5(nEBHOE), .Q6(nPCLOE),
    .Q7(nACCOE), .nOE(1'b0), .D0(_74138_rd_1_ny0), .D1(_74138_rd_1_ny1), .D2(_74138_rd_1_ny2),
    .D3(_74138_rd_1_ny3), .D4(_74138_rd_1_ny4), .D5(_74138_rd_1_ny5), .D6(_74138_rd_1_ny6),
    .D7(_74138_rd_1_ny7), .CLK(CLKLATCH), .VCC(1'b1), .GND(1'b0));
  _74574_RD _74574_rd_2 (
    .Q0(nEBLOE), .Q1(_74574_rd_2_q1), .Q2(nSTREGOE), .Q3(nEAHOE), .Q4(nXREGOE), .Q5(nYREGOE), .Q6(nEALOE),
    .Q7(nCONSTOE), .nOE(1'b0), .D0(_74138_rd_2_ny0), .D1(_74138_rd_2_ny1), .D2(_74138_rd_2_ny2),
    .D3(_74138_rd_2_ny3), .D4(_74138_rd_2_ny4), .D5(_74138_rd_2_ny5), .D6(_74138_rd_2_ny6),
    .D7(_74138_rd_2_ny7), .CLK(CLKLATCH), .VCC(1'b1), .GND(1'b0));
  _74574_RD _74574_rd_3 (
    .Q0(_74574_rd_3_q0), .Q1(nAREGCLK), .Q2(nBREGCLK), .Q3(nPCHCLK), .Q4(nSPREGCLK), .Q5(nEBHCLK),
    .Q6(nPCLCLK), .Q7(nACCCLK), .nOE(1'b0), .D0(_74138_rd_3_ny0), .D1(_74138_rd_3_ny1), .D2(_74138_rd_3_ny2),
    .D3(_74138_rd_3_ny3), .D4(_74138_rd_3_ny4), .D5(_74138_rd_3_ny5), .D6(_74138_rd_3_ny6),
    .D7(_74138_rd_3_ny7), .CLK(CLKLATCH), .VCC(1'b1), .GND(1'b0));
  _74574_RD _74574_rd_4 (
    .Q0(nEBLCLK), .Q1(_74574_rd_4_q1), .Q2(nSTREGCLK), .Q3(nEAHCLK), .Q4(nXREGCLK), .Q5(nYREGCLK),
    .Q6(nEALCLK), .Q7(_74574_rd_4_q7), .nOE(1'b0), .D0(_74138_rd_4_ny0), .D1(_74138_rd_4_ny1),
    .D2(_74138_rd_4_ny2), .D3(_74138_rd_4_ny3), .D4(_74138_rd_4_ny4), .D5(_74138_rd_4_ny5),
    .D6(_74138_rd_4_ny6), .D7(_74138_rd_4_ny7), .CLK(CLKLATCH), .VCC(1'b1), .GND(1'b0));
  LED nMAcc (.in(not_3_out));
  not not_3 (not_3_out, CtrlWord[21]);
  LED u_nPCHCLK (.in(not_4_out));
  LED ILoad (.in(CtrlWord[20]));
  not not_4 (not_4_out, CtrlWord[19]);
  LED u_nPCLCLK (.in(not_5_out));
  not not_5 (not_5_out, CtrlWord[18]);
  LED u_nSeqRst (.in(not_6_out));
  not not_6 (not_6_out, CtrlWord[17]);
  Seven_Seg_Hex seven_seg_hex_2 (.d(CtrlWord[11:8]), .dp(1'b0));
  // Probe ALUOp on CtrlWord[16:12]
  Seven_Seg_Hex seven_seg_hex_3 (.d(CtrlWord[3:0]), .dp(1'b0));
  Seven_Seg_Hex seven_seg_hex_4 (.d(CtrlWord[7:4]), .dp(1'b0));
  _74574_RD _74574_rd_5 (
    .Q0(Constant[0]), .Q1(Constant[1]), .Q2(Constant[2]), .Q3(Constant[3]), .Q4(ALUOp[0]), .Q5(ALUOp[1]),
    .Q6(ALUOp[2]), .Q7(ALUOp[3]), .nOE(1'b0), .D0(CtrlWord[8]), .D1(CtrlWord[9]), .D2(CtrlWord[10]),
    .D3(CtrlWord[11]), .D4(CtrlWord[12]), .D5(CtrlWord[13]), .D6(CtrlWord[14]), .D7(CtrlWord[15]),
    .CLK(CLKLATCH), .VCC(1'b1), .GND(1'b0));
  _74574_RD _74574_rd_6 (
    .Q0(ALUOp[4]), .Q1(nSEQRST), .Q2(nPCClockLow), .Q3(nPCClockHigh), .Q4(IREGLoad), .Q5(nMemAccess),
    .Q6(nMWrite), .Q7(nPCSel), .nOE(1'b0), .D0(CtrlWord[16]), .D1(CtrlWord[17]), .D2(CtrlWord[18]),
    .D3(CtrlWord[19]), .D4(CtrlWord[20]), .D5(CtrlWord[21]), .D6(CtrlWord[22]), .D7(CtrlWord[23]),
    .CLK(CLKLATCH), .VCC(1'b1), .GND(1'b0));
  _74574_RD _74574_rd_7 (
    .Q0(FLAG0), .Q1(FLAG1), .Q2(FLAG2), .Q3(CarryZERO), .Q4(CarryONE), .Q5(nUpdateNZ), .Q6(nUpdateC),
    .Q7(nUpdateV), .nOE(1'b0), .D0(CtrlWord[24]), .D1(CtrlWord[25]), .D2(CtrlWord[26]), .D3(CtrlWord[27]),
    .D4(CtrlWord[28]), .D5(CtrlWord[29]), .D6(CtrlWord[30]), .D7(CtrlWord[31]), .CLK(CLKLATCH), .VCC(1'b1),
    .GND(1'b0));
  _74574_RD _74574_rd_8 (
    .Q0(NoBCD), .Q1(nFlagInst), .Q2(nShiftRight), .Q3(nSBC), .Q4(nBITOP), .Q5(_74574_rd_8_q5),
    .Q6(_74574_rd_8_q6), .Q7(_74574_rd_8_q7), .nOE(1'b0), .D0(CtrlWord[32]), .D1(CtrlWord[33]),
    .D2(CtrlWord[34]), .D3(CtrlWord[35]), .D4(CtrlWord[36]), .D5(CtrlWord[37]), .D6(CtrlWord[38]),
    .D7(CtrlWord[39]), .CLK(CLKLATCH), .VCC(1'b1), .GND(1'b0));
  // Probe on CtrlWord
  not not_7 (CLKLATCH, CLK);

  // Notes on the sheet:
  //   INSTR: default 133
  //   STA (zeropage)
  //   00085: IREGLOAD | PCCLOCKLO | PCCLOCKHI | (HIZ << DRIVER) | MEMACCESS | PCSEL           BC000E
  //   00185: (EAH << LOAD) | (CONSTR << DRIVER)                                               0000BF
  //   00285: (EAL << LOAD) | (HIZ << DRIVER) | MEMACCESS | PCCLOCKLO | PCCLOCKHI | PCSEL      AC00EE
  //   00385: (AREG << DRIVER) | MEMACCESS | MWRITE | UCOUNTERRESET                            620001
  //   0-3
  //   4-7
  //   8-15
  //   16-23
  //   24-31
  //   32-39
endmodule
